# Fritzing sketch RfCompanion (saved by Fritzing 0.9.10b)
perfboards: 4
stripboards: 1

parts:
  A1 = Wemos S2 Mini [part_number="WeMos D1 Mini Lite"]
  M1 = cc1101 module
  OLED1 = OLED 128x64 I2C Monochrome Display  # not connected
  S1 = Tactile Switch Buttons - 12mm Square [package=tactile-pth-12mm]
  S2 = Tactile Switch Buttons - 12mm Square [package=tactile-pth-12mm]

nets:
  N1: A1.Pin_2, M1.pin_6
  N2: A1.Pin_3, A1.Pin_5, M1.pin_9, M1.pin_10
  N3: A1.Pin_4, M1.pin_7
  N4: A1.Pin_6, M1.pin_8
  N5: A1.Pin_7, M1.pin_5
  N6: A1.Pin_8, M1.pin_4
  N7: A1.Pin_18, A1.Pin_21, A1.Pin_22, A1.Pin_26, M1.pin_3, S1.1, S1.3, S2.1, S2.3
  N8: A1.Pin_19, S1.2, S1.4
  N9: A1.Pin_20, S2.2, S2.4

custom parts:
  Wemos S2 Mini: A mini wifi board based on the ESP32-S2FN4R2.
  cc1101 module: CC1101 rf module.
  Tactile Switch Buttons - 12mm Square: Medium-sized clicky momentary switches are standard input "buttons" on electronic projects. These work best in a PCB but can be used on a solderless breadboard as shown in this tutorial. The pins are normally open (disconnected) and when the button is pressed they are momentarily closed. They come in a pack of 10, they're pretty handy so you'll want to keep them around. You can find an EAGLE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
